// Logisim project control-logic.circ as structural Verilog: 2 circuits, main circuit control_logic
module control_logic (
  input  [31:0] Instruction,
  input  BrEq,
  input  BrLt,
  output PCSel,
  output RegWEn,
  output [2:0] ImmSel,
  output BrUn,
  output ASel,
  output BSel,
  output [3:0] ALUSel,
  output MemWEn,
  output [1:0] WBSel
);

  wire Iformat, not_1_out, not_2_out, not_3_out, not_4_out;
  wire [3:0] i_type_func3_handler_1_alusel, priority_encoder_1_out;
  wire [15:0] rom_1_data;

  not not_1 (not_1_out, Instruction[2]);
  not not_2 (not_2_out, Instruction[3]);
  not not_3 (not_3_out, Instruction[5]);
  not not_4 (not_4_out, Instruction[6]);
  and and_1 (Iformat, not_1_out, not_2_out, Instruction[4], not_3_out, not_4_out);
  I_Type_func3_handler i_type_func3_handler_1 (
    .func3(Instruction[14:12]), .func7_bit30(Instruction[30]), .ALUSel(i_type_func3_handler_1_alusel));
  Priority_Encoder #(.disabled("Z"), .select_enc(4)) priority_encoder_1 (
    .in0(Iformat), .out(priority_encoder_1_out));  // open: in1, in2, in3, in4, in5, in6, in7, in8, in9, in10, in11, in12, in13, in14, in15, gs, en_out, en_in
  Multiplexer #(.select(4), .width(4)) multiplexer_1 (
    .in0(i_type_func3_handler_1_alusel), .out(ALUSel), .sel(priority_encoder_1_out));  // open: in1, in2, in3, in4, in5, in6, in7, in8, in9, in10, in11, in12, in13, in14, in15
  ROM #(.addrWidth(6), .dataWidth(16)) rom_1 (.data(rom_1_data));  // open: addr

  assign RegWEn = 1'b1;

  // Other names for the same wires on the sheet: opcode[4:0] = Instruction[6:2]

  // Notes on the sheet:
  //   INPUTS to your circuit
  //   We only consider RV32 here so the 0 bit and 1 bit of instructions are not considered since they are all the same 
  //   DON'T CHANGE THE LOCATIONS OF THE INPUTS AND OUTPUTS!
  //   0: I-type
  //   OUTPUT from your circuit
  //   Connect ROM Input here ->
  //   ROM FOR CONTROL LOGIC
  //   This is only if you choose to do the ROM option
  //   CONNECT
  //   WIRE
  //   TO
  //   USE
  //   ROM
  //   Reminder: If using ROM, use combinational logic for PCSel
endmodule

module I_Type_func3_handler (
  input  [2:0] func3,
  input  func7_bit30,
  output [3:0] ALUSel
);

  wire and_1_out, not_1_out;
  wire [3:0] bit_extender_1_out;

  not not_1 (not_1_out, func3[1]);
  assign bit_extender_1_out = {{1{1'b0}}, func3};  // Bit_Extender bit_extender_1
  and and_1 (and_1_out, func3[0], not_1_out, func3[2], func7_bit30);
  Multiplexer #(.width(4)) multiplexer_1 (.in0(bit_extender_1_out), .in1(4'b1101), .out(ALUSel), .sel(and_1_out));

  // Notes on the sheet:
  //   If it is srai
endmodule
