// Logisim project cpu.circ as structural Verilog: 1 circuit, main circuit cpu
module cpu (
  input  clk,
  input  [31:0] Instruction,
  input  [31:0] MemReadData,
  output [31:0] MemAddress,
  output [31:0] ProgramCounter,
  output [31:0] ra,
  output [31:0] sp,
  output [31:0] t0,
  output [31:0] t1,
  output [31:0] t2,
  output [31:0] s0,
  output [31:0] s1,
  output [31:0] a0,
  output [3:0] MemWriteMask,
  output [31:0] MemWriteData
);

  wire ASel, BSel, RegWEn;
  wire [3:0] ALUSel;
  wire [31:0] adder_1_out, Imm, multiplexer_1_out, multiplexer_2_out, ReadDataA, ReadDataB, WriteData;

  Register #(.width(32)) PC (.D(adder_1_out), .clk(clk), .Q(ProgramCounter));  // open: en, clr
  Adder #(.width(32)) adder_1 (.a(ProgramCounter), .b(32'h4), .out(adder_1_out));  // open: cin, cout
  control_logic control_logic_1 (
    .Instruction(Instruction), .RegWEn(RegWEn), .ASel(ASel), .BSel(BSel), .ALUSel(ALUSel));  // open: BrEq, BrLt, PCSel, ImmSel, BrUn, MemWEn, WBSel
  regfile regfile_1 (
    .ReadIndex1(Instruction[19:15]), .ReadIndex2(Instruction[24:20]), .WriteIndex(Instruction[11:7]),
    .WriteData(WriteData), .RegWEn(RegWEn), .clk(clk), .ra(ra), .sp(sp), .t0(t0), .t1(t1), .t2(t2), .s0(s0),
    .s1(s1), .a0(a0), .ReadData1(ReadDataA), .ReadData2(ReadDataB));
  imm_gen imm_gen_1 (.Instruction(Instruction), .Immediate(Imm));  // open: ImmSel
  Multiplexer #(.width(32)) multiplexer_1 (.in0(ReadDataA), .in1(ProgramCounter), .out(multiplexer_1_out), .sel(ASel));
  Multiplexer #(.width(32)) multiplexer_2 (.in0(ReadDataB), .in1(Imm), .out(multiplexer_2_out), .sel(BSel));
  // branch_comp branch_comp_1: pin names not known
  alu alu_1 (.A(multiplexer_1_out), .B(multiplexer_2_out), .ALUSel(ALUSel), .ALUResult(WriteData));
  // partial_store partial_store_1: pin names not known
  // partial_load partial_load_1: pin names not known

  // Other names for the same wires on the sheet: WriteIndex[4:0] = Instruction[11:7];
  //   ReadIndex1[4:0] = Instruction[19:15]; ReadIndex2[4:0] = Instruction[24:20]

  // Notes on the sheet:
  //   To IMEM
  //   IMEM (do **NOT** move this)
  //   From IMEM
  //   Inputs/Outputs for testing. Do **NOT** move these.
  //   It is OK to move the PC, RegFile, ALU, MEM, Branch Comp, Imm Gen, Partial Load, Partial Store and Control Logic to wherever is most convenient for you when constructing your CPU, and to delete this text
  //   To DMEM
  //   DMEM (do **NOT** move this)
  //   From DMEM
endmodule
